# Fritzing sketch Door Controller RC522 (saved by Fritzing 0.9.3b)
circuit board: 11.4698cm x 5.56327cm
breadboards: 1

parts:
  Part1 = Arduino Uno (Rev3)
  LED1 = RGB LED - (4 legs) [package="5 mm [THT]"]
  R2 = Resistor [tolerance=±5% resistance=470k package=THT]
  Part2 = RFID-RC522-v2

nets:
  N1: Part1.D9_PWM, Part2.RST
  N2: Part1.D10_PWM/SS, Part2.SDA
  N3: Part1.D11_PWM/MOSI, Part2.MOSI
  N4: Part1.D12/MISO, Part2.MISO
  N5: Part1.D13/SCK, Part2.SCK
  N6: Part1.D5_PWM, LED1.blue_cathode
  N7: Part1.D6_PWM, LED1.green_cathode
  N8: Part1.D7, LED1.red_cathode
  3V3: Part1.3V3, Part2.3.3V
  GND: Part1.GND, R2.Pin_0, Part2.GND
  N9: LED1.common_anode, R2.Pin_1

custom parts:
  RFID-RC522-v2: A simple China made RFID-RC522 Reader; do check the pin labels, as this is a MFRC522 based clone.
